# Fritzing sketch schematics_VNH2SP30_MAX6818_FOR PCB (saved by Fritzing 0.9.6b)
circuit board: 8.46667cm x 5.64444cm
breadboards: 1

parts:
  Power_plug2 = Power plug
  J11 = female pin header, 2 pins [form="♀ (female)"]
  J14 = female pin header, 2 pins [form="♀ (female)"]
  JS3 = Generic Jumper Shunt
  C8 = Ceramic Capacitor [capacitance=100nF voltage=35V package="100 mil [THT, multilayer]"]
  C9 = Ceramic Capacitor [capacitance=100nF voltage=35V package="100 mil [THT, multilayer]"]
  J18 = AVR ISP 6 Pin [package=2x3_lock]
  U8 = atmega328 [package=dip]
  R15 = Resistor [tolerance=±5% power=0.25 resistance=4.7k package=THT]
  R16 = Resistor [tolerance=±5% power=0.25 resistance=4.7k package=THT]
  R17 = Resistor [tolerance=±5% power=0.25 resistance=4.7k package=THT]
  R18 = Resistor [tolerance=±5% power=0.25 resistance=4.7k package=THT]
  R19 = Resistor [tolerance=±5% power=0.25 resistance=4.7k package=THT]
  R20 = Resistor [tolerance=±5% power=0.25 resistance=4.7k package=THT]
  JP1 = Header 3 [package=jst-3-smd]
  MAX3 = DIP - 20 pins [package="DIP (Dual Inline) [THT]"]
  C10 = Ceramic Capacitor [capacitance=100nF voltage=35V package="100 mil [THT, multilayer]"]
  U9 = Header 1 [package=1x01_offset]
  U10 = Header 1 [package=1x01_offset]
  U11 = Header 4 [package=1x04-1mm-ra]
  U12 = Header 3 [package=1x03-1mm-ra]

nets:
  GND: Power_plug2.GND, C8.1, C9.1, J18.6, U8.GND, MAX3.1, C10.1, U10.1, U11.2, U11.3, U12.3
  VCC: Power_plug2.VCC, J18.2, U8.VCC, R19.Pin_1, MAX3.pin20, C10.0
  N1: J11.pin1, U8.A4, R20.Pin_0
  N2: J11.pin2, U8.A3, R18.Pin_0
  N3: J14.pin1, MAX3.pin4
  N4: J14.pin2, MAX3.pin3
  N5: JS3.pin1, C9.0, J18.5, R19.Pin_0
  N6: JS3.pin2, U8.RESET/PC6
  N7: C8.0, U8.AREF
  N8: J18.1, U8.D12
  N9: J18.3, U8.D13
  N10: J18.4, U8.D11_(PWM)
  N11: U8.XLAT1, MAX3.pin19
  N12: U8.XLAT2, MAX3.pin18
  N13: U8.D8, MAX3.pin17
  N14: U8.D9_(PWM), MAX3.pin16
  N15: U8.D10_(PWM), MAX3.pin15
  N16: U8.A0, R15.Pin_0
  N17: U8.A1, R16.Pin_0
  N18: U8.A2, R17.Pin_0
  N19: R15.Pin_1, U12.2
  N20: R16.Pin_1, U12.1
  N21: R17.Pin_1, JP1.3
  N22: R18.Pin_1, JP1.2
  N23: R20.Pin_1, JP1.1
  N24: MAX3.2, U11.1
  N25: MAX3.pin5, U9.1
  N26: MAX3.pin6, U11.4

custom parts:
  atmega328: Atmel ATmega328 microcontroller.
  DIP - 20 pins: A DIP stand-in part for whatever IC you want. With 20 pins on a 300mil dual inline package (DIP) footprint.
