# Fritzing sketch schematics_VNH2SP30 (saved by Fritzing 0.9.6b)
breadboards: 1

parts:
  U1 = atmega328 [package=dip]
  R1 = Resistor [tolerance=±5% power=0.25 resistance=4.7k package=THT]
  R2 = Resistor [tolerance=±5% power=0.25 resistance=4.7k package=THT]
  R3 = Resistor [tolerance=±5% power=0.25 resistance=4.7k package=THT]
  LED1 = LED - 5mm [color="Red (633nm)" current=0.030 package="5 mm [THT]"]
  LED2 = LED - 5mm [color="Red (633nm)" current=0.030 package="5 mm [THT]"]
  LED3 = LED - 5mm [color="Red (633nm)" current=0.030 package="5 mm [THT]"]
  M1 = DC Motor
  Open = Round Pushbutton
  Fully_closed = SWITCH-SPST-2 [package=switch-spst-vertical]
  Close = Round Pushbutton
  Emergency = Round Pushbutton
  Fully_open = SWITCH-SPST-2 [package=switch-spst-vertical]
  U3 = RF-LINK_TX [package=rf-link_tx]  # not connected
  U4 = RF-LINK_RX [package=rf-link_rx]
  ANT1 = Antenna
  U5 = VNH2SP30 [package=vnh2sp30]
  C1 = Ceramic Capacitor [capacitance=100nF voltage=35V package="100 mil [THT, multilayer]"]
  J1 = AVR ISP 6 Pin [package=2x3_lock]
  JS1 = Generic Jumper Shunt
  R4 = Resistor [tolerance=±5% power=0.25 resistance=10k package=THT]
  C2 = Ceramic Capacitor [capacitance=100nF voltage=35V package="100 mil [THT, multilayer]"]
  U6 = SRDA-06 [package=dip]
  U7 = atmega328 [package=dip]  # not connected
  U8 = SRDA-06 [package=dip]  # not connected
  J2 = AVR ISP 6 Pin [package=2x3_lock]  # not connected
  R5 = Resistor [tolerance=±5% power=0.25 resistance=4.7k package=THT]  # not connected
  R6 = Resistor [tolerance=±5% power=0.25 resistance=4.7k package=THT]  # not connected
  R7 = Resistor [tolerance=±5% power=0.25 resistance=4.7k package=THT]  # not connected
  C3 = Ceramic Capacitor [capacitance=100nF voltage=35V package="100 mil [THT, multilayer]"]  # not connected
  JS2 = Generic Jumper Shunt  # not connected
  J4 = female pin header, 2 pins [form="♀ (female)"]  # not connected
  J5 = female pin header, 2 pins [form="♀ (female)"]  # not connected
  J6 = female pin header, 2 pins [form="♀ (female)"]  # not connected
  J7 = female pin header, 2 pins [form="♀ (female)"]  # not connected
  J8 = female pin header, 2 pins [form="♀ (female)"]  # not connected
  J9 = female pin header, 2 pins [form="♀ (female)"]  # not connected
  R8 = Resistor [tolerance=±5% power=0.25 resistance=4.7k package=THT]  # not connected
  Power_plug1 = Power plug  # not connected

nets:
  N1: U1.RESET/PC6, JS1.pin2, R4.Pin_1, C2.0
  N2: U1.D0_(RX)/PD0, U4.DATA
  5V: U1.VCC, U4.+5V, U5.EN_DIAA, U5.PWM, U5.EN_DIAB, J1.2, R4.Pin_0, U6.Pin_3
  GND: U1.GND, LED1.cathode, LED2.cathode, LED3.cathode, Open.leg0, Fully_closed.P, Close.leg0, Emergency.leg0, Fully_open.P, U4.GND, U5.GNDB, U5.GNDA, C1.1, J1.6, C2.1, U6.Pin_8
  N3: U1.XLAT1, Fully_closed.O, U6.Pin_1
  N4: U1.XLAT2, Emergency.leg1, U6.Pin_2
  N5: U1.D8, Open.leg1, U6.Pin_4
  N6: U1.D9_(PWM), Close.leg1, U6.Pin_6
  N7: U1.D10_(PWM), Fully_open.O, U6.Pin_5
  N8: U1.D11_(PWM), J1.4
  N9: U1.D12, J1.1
  N10: U1.D13, J1.3
  N11: U1.AREF, C1.0
  N12: U1.A0, R1.Pin_0
  N13: U1.A1, R2.Pin_0
  N14: U1.A2, R3.Pin_0
  N15: U1.A3, U5.INB
  N16: U1.A4, U5.INA
  N17: R1.Pin_1, LED1.anode
  N18: R2.Pin_1, LED2.anode
  N19: R3.Pin_1, LED3.anode
  N20: M1.pin_1, U5.OUTA
  N21: M1.pin_2, U5.OUTB
  N22: U4.ANT, ANT1.antenna_lead
  12V: U5.VCC
  N23: J1.5, JS1.pin1

notes:
  R1, R2, R3 = 330 Ohm
  Garage door state machine

custom parts:
  atmega328: Atmel ATmega328 microcontroller.
  SRDA-06: Low Capacitance TVS Array
