# Fritzing sketch schematics_VNH2SP30_MAX6818 (saved by Fritzing 0.9.6b)
breadboards: 1

parts:
  U1 = atmega328 [package=dip]
  R1 = Resistor [tolerance=±5% power=0.25 resistance=4.7k package=THT]
  R2 = Resistor [tolerance=±5% power=0.25 resistance=4.7k package=THT]
  R3 = Resistor [tolerance=±5% power=0.25 resistance=4.7k package=THT]
  M1 = DC Motor
  Open = Round Pushbutton
  Fully_closed = SWITCH-SPST-2 [package=switch-spst-vertical]
  Close = Round Pushbutton
  Emergency = Round Pushbutton
  Fully_open = SWITCH-SPST-2 [package=switch-spst-vertical]
  U3 = RF-LINK_TX [package=rf-link_tx]  # not connected
  U4 = RF-LINK_RX [package=rf-link_rx]
  ANT1 = Antenna
  U5 = VNH2SP30 [package=vnh2sp30]
  C1 = Ceramic Capacitor [capacitance=100nF voltage=35V package="100 mil [THT, multilayer]"]
  J1 = AVR ISP 6 Pin [package=2x3_lock]
  JS1 = Generic Jumper Shunt
  U7 = atmega328 [package=dip]  # not connected
  J2 = AVR ISP 6 Pin [package=2x3_lock]  # not connected
  R5 = Resistor [tolerance=±5% power=0.25 resistance=4.7k package=THT]  # not connected
  R6 = Resistor [tolerance=±5% power=0.25 resistance=4.7k package=THT]  # not connected
  R7 = Resistor [tolerance=±5% power=0.25 resistance=4.7k package=THT]  # not connected
  C3 = Ceramic Capacitor [capacitance=100nF voltage=35V package="100 mil [THT, multilayer]"]  # not connected
  JS2 = Generic Jumper Shunt  # not connected
  J4 = female pin header, 2 pins [form="♀ (female)"]  # not connected
  J5 = female pin header, 2 pins [form="♀ (female)"]  # not connected
  J6 = female pin header, 2 pins [form="♀ (female)"]  # not connected
  J7 = female pin header, 2 pins [form="♀ (female)"]  # not connected
  J8 = female pin header, 2 pins [form="♀ (female)"]  # not connected
  J9 = female pin header, 2 pins [form="♀ (female)"]  # not connected
  Power_plug1 = Power plug  # not connected
  MAX1 = DIP - 20 pins [package="DIP (Dual Inline) [THT]"]
  MAX2 = DIP - 20 pins [package="DIP (Dual Inline) [THT]"]  # not connected
  C4 = Ceramic Capacitor [capacitance=100nF voltage=35V package="100 mil [THT, multilayer]"]
  R9 = Resistor [tolerance=±5% power=0.25 resistance=4.7k package=THT]
  R10 = Resistor [tolerance=±5% power=0.25 resistance=4.7k package=THT]
  Fully_Closed = LED - 5mm [color="Red (633nm)" current=0.030 package="5 mm [THT]"]
  Fully_Open = LED - 5mm [color="Red (633nm)" current=0.030 package="5 mm [THT]"]
  C5 = Ceramic Capacitor [capacitance=100nF voltage=35V package="100 mil [THT, multilayer]"]
  R11 = Resistor [tolerance=±5% power=0.25 resistance=10k package=THT]
  R12 = Resistor [tolerance=±5% power=0.25 resistance=4.7k package=THT]  # not connected
  R13 = Resistor [tolerance=±5% power=0.25 resistance=4.7k package=THT]  # not connected
  J10 = female pin header, 2 pins [form="♀ (female)"]  # not connected
  C6 = Ceramic Capacitor [capacitance=100nF voltage=35V package="100 mil [THT, multilayer]"]  # not connected
  R14 = Resistor [tolerance=±5% power=0.25 resistance=4.7k package=THT]  # not connected
  C7 = Ceramic Capacitor [capacitance=100nF voltage=35V package="100 mil [THT, multilayer]"]  # not connected

nets:
  N1: U1.RESET/PC6, JS1.pin2
  N2: U1.D0_(RX)/PD0, U4.DATA
  5V: U1.VCC, U4.+5V, U5.EN_DIAA, U5.PWM, U5.EN_DIAB, J1.2, MAX1.pin20, C4.0, R11.Pin_1
  GND: U1.GND, Open.leg0, Fully_closed.P, Close.leg0, Emergency.leg0, Fully_open.P, U4.GND, U5.GNDB, U5.GNDA, C1.1, J1.6, MAX1.1, MAX1.pin10, C4.1, Fully_Closed.cathode, Fully_Open.cathode, C5.1
  N3: U1.XLAT1, MAX1.pin19
  N4: U1.XLAT2, MAX1.pin18
  N5: U1.D8, MAX1.pin17
  N6: U1.D9_(PWM), MAX1.pin16
  N7: U1.D10_(PWM), MAX1.pin15
  N8: U1.D11_(PWM), J1.4
  N9: U1.D12, J1.1
  N10: U1.D13, J1.3
  N11: U1.AREF, C1.0
  N12: U1.A0, R1.Pin_0
  N13: U1.A1, R2.Pin_0
  N14: U1.A2, R3.Pin_0
  N15: U1.A3, U5.INB, R9.Pin_0
  N16: U1.A4, U5.INA, R10.Pin_0
  N17: M1.pin_1, U5.OUTA
  N18: M1.pin_2, U5.OUTB
  N19: Open.leg1, MAX1.pin4
  N20: Fully_closed.O, MAX1.2
  N21: Close.leg1, MAX1.pin5
  N22: Emergency.leg1, MAX1.pin3
  N23: Fully_open.O, MAX1.pin6
  N24: U4.ANT, ANT1.antenna_lead
  12V: U5.VCC
  N25: J1.5, JS1.pin1, C5.0, R11.Pin_0

notes:
  R1, R2, R3, R9, R10 = 330 Ohm
  Garage door state machine
  Diagnostics

custom parts:
  atmega328: Atmel ATmega328 microcontroller.
  DIP - 20 pins: A DIP stand-in part for whatever IC you want. With 20 pins on a 300mil dual inline package (DIP) footprint.
