# Fritzing sketch schematics_VNH2SP30_MAX6818_FOR PCB (saved by Fritzing 0.9.6b)
circuit board: 8.46667cm x 5.64444cm
breadboards: 1

parts:
  MAX3 = DIP - 20 pins [package="DIP (Dual Inline) [THT]"]
  Power_plug2 = Power plug
  J11 = female pin header, 2 pins [form="♀ (female)"]
  J12 = female pin header, 2 pins [form="♀ (female)"]
  J14 = female pin header, 2 pins [form="♀ (female)"]
  J16 = female pin header, 2 pins [form="♀ (female)"]
  J17 = female pin header, 2 pins [form="♀ (female)"]
  JS3 = Generic Jumper Shunt
  C8 = Ceramic Capacitor [capacitance=100nF voltage=35V package="100 mil [THT, multilayer]"]
  C9 = Ceramic Capacitor [capacitance=100nF voltage=35V package="100 mil [THT, multilayer]"]
  C10 = Ceramic Capacitor [capacitance=100nF voltage=35V package="100 mil [THT, multilayer]"]
  J18 = AVR ISP 6 Pin [package=2x3_lock]
  U8 = atmega328 [package=dip]
  R15 = Resistor [tolerance=±5% power=0.25 resistance=4.7k package=THT]
  R16 = Resistor [tolerance=±5% power=0.25 resistance=4.7k package=THT]
  R17 = Resistor [tolerance=±5% power=0.25 resistance=4.7k package=THT]
  R18 = Resistor [tolerance=±5% power=0.25 resistance=4.7k package=THT]
  R19 = Resistor [tolerance=±5% power=0.25 resistance=4.7k package=THT]
  R20 = Resistor [tolerance=±5% power=0.25 resistance=4.7k package=THT]
  JP1 = Header 3 [package=jst-3-smd]

nets:
  GND: MAX3.1, Power_plug2.GND, C8.1, C9.1, C10.1, J18.6, U8.GND
  N1: MAX3.2, J14.pin2
  N2: MAX3.pin3, J14.pin1
  N3: MAX3.pin4, JP1.3
  N4: MAX3.pin5, JP1.2
  N5: MAX3.pin6, JP1.1
  N6: MAX3.pin15, U8.D10_(PWM)
  N7: MAX3.pin16, U8.D9_(PWM)
  N8: MAX3.pin17, U8.D8
  N9: MAX3.pin18, U8.XLAT2
  N10: MAX3.pin19, U8.XLAT1
  VCC: MAX3.pin20, Power_plug2.VCC, C10.0, J18.2, U8.VCC, R19.Pin_1
  N11: J11.pin1, U8.A4, R20.Pin_0
  N12: J11.pin2, U8.A3, R18.Pin_0
  N13: J12.pin1, R20.Pin_1
  N14: J12.pin2, R18.Pin_1
  N15: J16.pin2, R15.Pin_1
  N16: J17.pin1, R17.Pin_1
  N17: J17.pin2, R16.Pin_1
  N18: JS3.pin1, C9.0, J18.5, R19.Pin_0
  N19: JS3.pin2, U8.RESET/PC6
  N20: C8.0, U8.AREF
  N21: J18.1, U8.D12
  N22: J18.3, U8.D13
  N23: J18.4, U8.D11_(PWM)
  N24: U8.A0, R15.Pin_0
  N25: U8.A1, R16.Pin_0
  N26: U8.A2, R17.Pin_0

custom parts:
  DIP - 20 pins: A DIP stand-in part for whatever IC you want. With 20 pins on a 300mil dual inline package (DIP) footprint.
  atmega328: Atmel ATmega328 microcontroller.
