# Fritzing sketch sevenSegmentWithAttiny_4313 (saved by Fritzing 0.9.6b)
breadboards: 1

parts:
  MICRICHIP_ATtiny1 = ATtiny [package=THT]
  U1 = 7-SEGMENT-4DIGIT [package=7-segment-4digit_longpads_for_pogobed]

nets:
  N1: MICRICHIP_ATtiny1.(PB1)_(MOSI), U1.2
  N2: MICRICHIP_ATtiny1.(PB2), U1.3
  N3: MICRICHIP_ATtiny1.Gnd, U1.8
  N4: MICRICHIP_ATtiny1.(PB4), U1.16
  N5: MICRICHIP_ATtiny1.(P6), U1.11
  N6: MICRICHIP_ATtiny1.(P5), U1.9
  N7: MICRICHIP_ATtiny1.(P4), U1.4
  N8: MICRICHIP_ATtiny1.AVcc, U1.6
  N9: MICRICHIP_ATtiny1.AGND, U1.1
  N10: MICRICHIP_ATtiny1.(P3), U1.14
  N11: MICRICHIP_ATtiny1.(P2), U1.15

custom parts:
  ATtiny: ATMEL ATtiny861
